# Fritzing sketch stepper-motor (saved by Fritzing 0.9.10b)
breadboards: 1

parts:
  M2 = Stepper Motor - Bipolar  # not connected
  DRV_1 = DRV 8825 Stepper Motor Carrier, High Current [part_number="DRV 8825"]  # not connected
  Part1 = Arduino Uno (Rev3)  # not connected
  C1 = Electrolytic Capacitor [capacitance=100µF voltage=35V package="200 mil [THT, electrolytic]"]
  VCC1 = Battery block 9V

nets:
  N1: C1.-, VCC1.+
  N2: C1.+, VCC1.-
